// Digital circuit Main.dig as structural Verilog
module Main (
  input  Clock
);

  wire [1:0] Fetch_pcra, Stage_1_fetch_suppress, undriven_5;
  wire [2:0] Control_const, undriven_4;
  wire [3:0] alu_1_p7, Control_gpr_a, Control_gpr_b, Control_gpr_c, Control_gpr_d, Control_mem, undriven_3;
  wire [5:0] Control_dev_load;
  wire [6:0] Control_dev_assert, Control_di, Control_pcra0, Control_pcra1, Control_si, Control_sp, Reset_out,
       undriven_2;
  wire [7:0] A_i, A_lhs, A_rhs, B_i, C_i, Constant_i, Control_xfer_2, D_i, DI_i, Fetch_pipeout,
       memory_bridge_1_mem, PCRA0_i, PCRA1_i, SI_i, SP_i, Stage_1_pipeout, transfer_register_1_main, undriven;
  wire [15:0] PCRA0_addr, PCRA0_xfer, transfer_register_1_i;

  Address_Register PCRA0 (.XFER(PCRA0_xfer), .ADDR(PCRA0_addr), .Control(Control_pcra0), .I(PCRA0_i));
  Address_Register PCRA1 (.XFER(PCRA0_xfer), .ADDR(PCRA0_addr), .Control(Control_pcra1), .I(PCRA1_i));
  Address_Register SP (.XFER(PCRA0_xfer), .ADDR(PCRA0_addr), .Control(Control_sp), .I(SP_i));
  Address_Register SI (.XFER(PCRA0_xfer), .ADDR(PCRA0_addr), .Control(Control_si), .I(SI_i));
  Address_Register DI (.XFER(PCRA0_xfer), .ADDR(PCRA0_addr), .Control(Control_di), .I(DI_i));
  Transfer_Register transfer_register_1 (
    .MAIN(transfer_register_1_main), .XFER(PCRA0_xfer), .ADDR(PCRA0_addr), .C(Control_xfer_2),
    .I(transfer_register_1_i));
  Memory memory_1 (.ADDR(PCRA0_addr), .Control(Control_mem), .MEM(memory_bridge_1_mem));
  // Probe on PCRA0_i
  // Probe on PCRA1_i
  // Probe on SP_i
  // Probe on SI_i
  // Probe on DI_i
  // Probe ADDR on PCRA0_addr
  // Probe XFER on PCRA0_xfer
  // Probe MEM on memory_bridge_1_mem
  Bus_Control Control (
    .Dev_Load(Control_dev_load), .Main(undriven), .Xfer(undriven_2), .Clock(Clock), .Reset(Reset_out[6]),
    .Inc({undriven_5, Fetch_pcra}), .ALU_Assert(undriven_3), .Addr_Assert(undriven_4),
    .Dev_Assert(Control_dev_assert), .PCRA0(Control_pcra0), .PCRA1(Control_pcra1), .SP(Control_sp),
    .SI(Control_si), .DI(Control_di), .GPR_A(Control_gpr_a), .GPR_B(Control_gpr_b), .GPR_C(Control_gpr_c),
    .GPR_D(Control_gpr_d), .Const(Control_const), .XFER_2(Control_xfer_2), .Mem(Control_mem));
  // Probe on transfer_register_1_i
  GPR A (.RHS(A_rhs), .LHS(A_lhs), .MAIN(transfer_register_1_main), .Control(Control_gpr_a), .I(A_i));
  GPR B (.RHS(A_rhs), .LHS(A_lhs), .MAIN(transfer_register_1_main), .Control(Control_gpr_b), .I(B_i));
  GPR C (.RHS(A_rhs), .LHS(A_lhs), .MAIN(transfer_register_1_main), .Control(Control_gpr_c), .I(C_i));
  GPR D (.RHS(A_rhs), .LHS(A_lhs), .MAIN(transfer_register_1_main), .Control(Control_gpr_d), .I(D_i));
  Constant_Register Constant (
    .Control(Control_const), .MEM(memory_bridge_1_mem), .MAIN(transfer_register_1_main), .I(Constant_i));
  Memory_Bridge memory_bridge_1 (.MAIN(transfer_register_1_main), .MEM(memory_bridge_1_mem), .Control(Control_mem));
  // Probe on A_i
  // Probe on B_i
  // Probe on C_i
  // Probe on D_i
  // Probe on Constant_i
  // Probe RHS on A_rhs
  // Probe LHS on A_lhs
  // Probe MAIN on transfer_register_1_main
  // ALU alu_1: pin names not known; wires that end beside it: Control_dev_assert[0], A_rhs, A_lhs, transfer_register_1_main, Reset_out[4:0], Clock, alu_1_p7
  Stage_2 Stage_2 (
    .Flags(Reset_out), .Clock(Clock), .PipeIn(Stage_1_pipeout), .Main(undriven), .SPSIDI(undriven_5),
    .Addr(undriven_4), .Bus_Request(Stage_1_fetch_suppress[1]), .PCRA_Flip(Reset_out[5]));  // open: Break
  Stage_1 Stage_1 (
    .ALU_Bus(undriven_3), .ALU_Ops(alu_1_p7), .Xfer(undriven_2), .Fetch_suppress(Stage_1_fetch_suppress[0]),
    .Control(Stage_1_fetch_suppress), .PipeOut(Stage_1_pipeout), .Flags(Reset_out), .Clock(Clock),
    .PipeIn(Fetch_pipeout));
  Fetch Fetch (
    .MEM(memory_bridge_1_mem), .Flags(Reset_out), .Clock(Clock), .PCRA(Fetch_pcra),
    .Control(Stage_1_fetch_suppress), .PipeOut(Fetch_pipeout));
  Button #(.activeLow("true")) Reset (.out(Reset_out[6]));
  Terminal terminal_1 (.D(transfer_register_1_main), .C(Clock), .Load(Control_dev_load[0]));
  // Probe Inc on {undriven_5, Fetch_pcra}
  // Probe Addr on undriven_4
  // Probe ALU Ops on alu_1_p7
  // Probe ALU Bus on undriven_3
  // Probe Xfer on undriven_2
  // Probe Main on undriven
  // Probe Stage2 on Stage_1_pipeout
  // Probe Stage1 on Fetch_pipeout

  // Notes on the sheet:
  //   Clock: Hz: 10
  //   contents of ROM (hex, n*v repeats v):
  //   0,5,1,6,0,29,5,31,6,0,27,5,14,6,0,5c,0,2a,5f,60,2a,72,76,77,0,0,0,5,24,6,0,29,5,2b, 6,0,5b,
  //   fc,5f,65,39,5f,71,7d,7c,78,29,5e,0,48,65,6c,6c,6f,20,57,6f,72,6c,64,21,5c, 6e
  //   contents of Stage 1-B (hex, n*v repeats v):
  //   0,88,88,88,88,88,88,0,0,0,0,0,0,0,0,0,0,0,0,0,0,0,0,0,0,0,0,0,0,0,0,0,0,0,0,62,26, 63,36,64,
  //   46,65,56,45,54,34,35,0,a,b,c,d,0,0,0,0,0,0,0,0,0,0,0,0,0,0,0,0,0,0,0,0,0, 0,0,0,0,0,0,0,0,0,
  //   0,0,0,0,0,0,0,0,0,0,62,52,0,0,61,0,61,0,61,0,61,0,61,0,61,0,61, 0,61,0,61,51,b,b,b,b,b,b,0,
  //   0,0,0,0,0,0,0,0,0,0,0,0,0,0,0,0,0,0,0,0,0,0,0,0,0,0,0, 0,0,0,0,0,0,0,0,0,0,0,0,0,0,0,0,0,0,
  //   0,0,0,0,0,0,0,0,0,0,0,0,0,0,0,0,0,0,0,0,0,0,0, 0,0,0,0,0,0,0,0,0,0,0,0,0,0,0,0,0,0,0,0,0,0,
  //   0,0,0,0,0,0,0,0,0,0,0,0,0,0,0,0,0,0,0, 0,0,0,0,0,0,0,0,0,0,0,0,0,0,0,0,0,0,0,0,0,0,0,0,0,0,
  //   0,88,88,88,88,88,88,0,0,0,0,0, 0,0,0,0,0,0,0,0,0,0,0,0,0,0,0,0,0,0,0,0,0,0,0,62,26,63,36,64,
  //   46,65,56,45,54,34,35, 0,a,b,c,d,0,0,0,0,0,0,0,0,0,0,0,0,0,0,0,0,0,0,0,0,0,0,0,0,0,0,0,0,0,0,
  //   0,0,0,0,0,0, 0,0,0,0,62,52,0,0,61,61,0,0,61,0,61,0,61,0,61,61,0,61,61,0,61,51,b,b,b,b,b,b,0,
  //   0, 0,0,0,0,0,0,0,0,0,0,0,0,0,0,0,0,0,0,0,0,0,0,0,0,0,0,0,0,0,0,0,0,0,0,0,0,0,0,0,0,0, 0,0,0,
  //   0,0,0,0,0,0,0,0,0,0,0,0,0,0,0,0,0,0,0,0,0,0,0,0,0,0,0,0,0,0,0,0,0,0,0,0,0,0, 0,0,0,0,0,0,0,
  //   0,0,0,0,0,0,0,0,0,0,0,0,0,0,0,0,0,0,0,0,0,0,0,0,0,0,0,0,0,0,0,0,0,0, 0,0,0,0,0,0,0,0,0,0,0,
  //   0,88,88,88,88,88,88,0,0,0,0,0,0,0,0,0,0,0,0,0,0,0,0,0,0,0,0, 0,0,0,0,0,0,0,0,62,26,63,36,64,
  //   46,65,56,45,54,34,35,0,a,b,c,d,0,0,0,0,0,0,0,0,0,0, 0,0,0,0,0,0,0,0,0,0,0,0,0,0,0,0,0,0,0,0,
  //   0,0,0,0,0,0,0,0,0,0,62,52,0,0,61,0,61,61, 0,0,61,0,61,0,61,61,0,61,0,0,61,51,b,b,b,b,b,b,0,
  //   0,0,0,0,0,0,0,0,0,0,0,0,0,0,0,0, 0,0,0,0,0,0,0,0,0,0,0,0,0,0,0,0,0,0,0,0,0,0,0,0,0,0,0,0,0,
  //   0,0,0,0,0,0,0,0,0,0,0,0, 0,0,0,0,0,0,0,0,0,0,0,0,0,0,0,0,0,0,0,0,0,0,0,0,0,0,0,0,0,0,0,0,0,
  //   0,0,0,0,0,0,0,0, 0,0,0,0,0,0,0,0,0,0,0,0,0,0,0,0,0,0,0,0,0,0,0,0,0,0,0,0,0,0,0,0,0,0,0,0,0,
  //   0,88,88, 88,88,88,88,0,0,0,0,0,0,0,0,0,0,0,0,0,0,0,0,0,0,0,0,0,0,0,0,0,0,0,0,62,26,63,36,64,
  //    46,65,56,45,54,34,35,0,a,b,c,d,0,0,0,0,0,0,0,0,0,0,0,0,0,0,0,0,0,0,0,0,0,0,0,0,0, 0,0,0,0,
  //   0,0,0,0,0,0,0,0,0,0,0,62,52,0,0,61,61,0,61,0,0,61,0,61,0,61,0,61,0,0,0,61, 51,b,b,b,b,b,b,0,
  //   0,0,0,0,0,0,0,0,0,0,0,0,0,0,0,0,0,0,0,0,0,0,0,0,0,0,0,0,0,0,0,0, 0,0,0,0,0,0,0,0,0,0,0,0,0,
  //   0,0,0,0,0,0,0,0,0,0,0,0,0,0,0,0,0,0,0,0,0,0,0,0,0,0,0,0, 0,0,0,0,0,0,0,0,0,0,0,0,0,0,0,0,0,
  //   0,0,0,0,0,0,0,0,0,0,0,0,0,0,0,0,0,0,0,0,0,0,0,0, 0,0,0,0,0,0,0,0,0,0,0,0,0,0,0,0,0,0,0,0,0,
  //   0,88,88,88,88,88,88,0,0,0,0,0,0,0,0,0,0, 0,0,0,0,0,0,0,0,0,0,0,0,0,0,0,0,0,0,62,26,63,36,64,
  //   46,65,56,45,54,34,35,0,a,b,c,d, 0,0,0,0,0,0,0,0,0,0,0,0,0,0,0,0,0,0,0,0,0,0,0,0,0,0,0,0,0,0,
  //   0,0,0,0,0,0,0,0,0,0,62, 52,0,0,61,0,61,0,61,61,0,0,61,61,0,0,61,61,0,0,61,51,b,b,b,b,b,b,0,
  //   0,0,0,0,0,0,0, 0,0,0,0,0,0,0,0,0,0,0,0,0,0,0,0,0,0,0,0,0,0,0,0,0,0,0,0,0,0,0,0,0,0,0,0,0,0,
  //   0,0,0, 0,0,0,0,0,0,0,0,0,0,0,0,0,0,0,0,0,0,0,0,0,0,0,0,0,0,0,0,0,0,0,0,0,0,0,0,0,0,0,0,0, 0,
  //   0,0,0,0,0,0,0,0,0,0,0,0,0,0,0,0,0,0,0,0,0,0,0,0,0,0,0,0,0,0,0,0,0,0,0,0,0,0,0,0, 0,0,0,0,0,
  //   0,88,88,88,88,88,88,0,0,0,0,0,0,0,0,0,0,0,0,0,0,0,0,0,0,0,0,0,0,0,0,0,0, 0,0,62,26,63,36,64,
  //   46,65,56,45,54,34,35,0,a,b,c,d,0,0,0,0,0,0,0,0,0,0,0,0,0,0,0,0, 0,0,0,0,0,0,0,0,0,0,0,0,0,0,
  //   0,0,0,0,0,0,0,0,0,0,62,52,0,0,61,61,0,0,61,61,0,0,61, 61,0,61,0,61,0,0,61,51,b,b,b,b,b,b,0,
  //   0,0,0,0,0,0,0,0,0,0,0,0,0,0,0,0,0,0,0,0,0,0, 0,0,0,0,0,0,0,0,0,0,0,0,0,0,0,0,0,0,0,0,0,0,0,
  //   0,0,0,0,0,0,0,0,0,0,0,0,0,0,0,0,0,0, 0,0,0,0,0,0,0,0,0,0,0,0,0,0,0,0,0,0,0,0,0,0,0,0,0,0,0,
  //   0,0,0,0,0,0,0,0,0,0,0,0,0,0, 0,0,0,0,0,0,0,0,0,0,0,0,0,0,0,0,0,0,0,0,0,0,0,0,0,0,0,0,0,0,0,
  //   0,88,88,88,88,88,88, 0,0,0,0,0,0,0,0,0,0,0,0,0,0,0,0,0,0,0,0,0,0,0,0,0,0,0,0,62,26,63,36,64,
  //   46,65,56,45, 54,34,35,0,a,b,c,d,0,0,0,0,0,0,0,0,0,0,0,0,0,0,0,0,0,0,0,0,0,0,0,0,0,0,0,0,0,0,
  //   0, 0,0,0,0,0,0,0,0,0,62,52,0,0,61,0,61,61,0,61,0,0,61,61,0,61,0,61,0,0,61,51,b,b,b,b, b,b,0,
  //   0,0,0,0,0,0,0,0,0,0,0,0,0,0,0,0,0,0,0,0,0,0,0,0,0,0,0,0,0,0,0,0,0,0,0,0,0,0, 0,0,0,0,0,0,0,
  //   0,0,0,0,0,0,0,0,0,0,0,0,0,0,0,0,0,0,0,0,0,0,0,0,0,0,0,0,0,0,0,0,0,0, 0,0,0,0,0,0,0,0,0,0,0,
  //   0,0,0,0,0,0,0,0,0,0,0,0,0,0,0,0,0,0,0,0,0,0,0,0,0,0,0,0,0,0, 0,0,0,0,0,0,0,0,0,0,0,0,0,0,0,
  //   0,88,88,88,88,88,88,0,0,0,0,0,0,0,0,0,0,0,0,0,0,0,0, 0,0,0,0,0,0,0,0,0,0,0,0,62,26,63,36,64,
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  //   contents of Stage 2-A (hex, n*v repeats v):
  //   0,15,25,35,45,65,75,12,13,14,21,23,24,31,32,34,41,42,43,61,62,63,64,71,72,73,74,16, 26,36,46,
  //   17,27,37,47,0,0,0,0,0,0,0,0,0,0,0,0,0,0,0,0,0,0,0,0,e1,d1,91,0,0,0,0,0,0, 1f,2f,3f,4f,1f,2f,
  //   3f,4f,1f,2f,3f,4f,f1,f2,f3,f4,f1,f2,f3,f4,f1,f2,f3,f4,0,0,0,1f, 0,0,0,0,0,0,0,0,0,0,0,0,0,0,
  //   0,0,0,0,0,0,0,0,f1,f2,f3,f4,f6,f7,1f,2f,3f,4f,6f,7f,0, 0,18,28,38,48,18,28,38,48,18,18,18,28,
  //   28,28,38,38,38,48,48,48,18,18,18,28,28,28,38, 38,38,48,48,48,18,28,38,48,18,28,38,48,18,18,
  //   18,28,28,28,38,38,38,48,48,48,18,18, 18,28,28,28,38,38,38,48,48,48,18,28,38,48,18,18,18,28,
  //   28,28,38,38,38,48,48,48,18, 18,18,28,28,28,38,38,38,48,48,48,18,18,18,28,28,28,38,38,38,48,
  //   48,48,18,28,38,48, 18,28,38,48,0,0,0,0,0,0,0,0,0,0,0,0,0,0,0,0,0,15,25,35,45,65,75,12,13,14,
  //   21,23,24, 31,32,34,41,42,43,61,62,63,64,71,72,73,74,16,26,36,46,17,27,37,47,0,0,0,0,0,0,0,0,
  //    0,0,0,0,0,0,0,0,0,0,0,0,e1,d1,91,0,0,0,0,0,0,1f,2f,3f,4f,1f,2f,3f,4f,1f,2f,3f,4f, f1,f2,f3,
  //   f4,f1,f2,f3,f4,f1,f2,f3,f4,0,0,0,1f,0,0,0,0,0,0,0,0,0,0,0,0,0,0,0,0,0,0, 0,0,0,0,f1,f2,f3,f4,
  //   f6,f7,1f,2f,3f,4f,6f,7f,0,0,18,28,38,48,18,28,38,48,18,18,18, 28,28,28,38,38,38,48,48,48,18,
  //   18,18,28,28,28,38,38,38,48,48,48,18,28,38,48,18,28, 38,48,18,18,18,28,28,28,38,38,38,48,48,
  //   48,18,18,18,28,28,28,38,38,38,48,48,48,18, 28,38,48,18,18,18,28,28,28,38,38,38,48,48,48,18,
  //   18,18,28,28,28,38,38,38,48,48,48, 18,18,18,28,28,28,38,38,38,48,48,48,18,28,38,48,18,28,38,
  //   48,0,0,0,0,0,0,0,0,0,0,0, 0,0,0,0,0,0,15,25,35,45,65,75,12,13,14,21,23,24,31,32,34,41,42,43,
  //   61,62,63,64,71, 72,73,74,16,26,36,46,17,27,37,47,0,0,0,0,0,0,0,0,0,0,0,0,0,0,0,0,0,0,0,0,e1,
  //   d1,91, 0,0,0,0,0,0,1f,2f,3f,4f,1f,2f,3f,4f,1f,2f,3f,4f,f1,f2,f3,f4,f1,f2,f3,f4,f1,f2,f3, f4,
  //   0,0,0,1f,0,0,0,0,0,0,0,0,0,0,0,0,0,0,0,0,0,0,0,0,0,0,f1,f2,f3,f4,f6,f7,1f,2f,3f, 4f,6f,7f,0,
  //   0,18,28,38,48,18,28,38,48,18,18,18,28,28,28,38,38,38,48,48,48,18,18,18, 28,28,28,38,38,38,48,
  //   48,48,18,28,38,48,18,28,38,48,18,18,18,28,28,28,38,38,38,48, 48,48,18,18,18,28,28,28,38,38,
  //   38,48,48,48,18,28,38,48,18,18,18,28,28,28,38,38,38, 48,48,48,18,18,18,28,28,28,38,38,38,48,
  //   48,48,18,18,18,28,28,28,38,38,38,48,48,48, 18,28,38,48,18,28,38,48,0,0,0,0,0,0,0,0,0,0,0,0,
  //   0,0,0,0,0,15,25,35,45,65,75,12,13, 14,21,23,24,31,32,34,41,42,43,61,62,63,64,71,72,73,74,16,
  //   26,36,46,17,27,37,47,0,0, 0,0,0,0,0,0,0,0,0,0,0,0,0,0,0,0,0,0,e1,d1,91,0,0,0,0,0,0,1f,2f,3f,
  //   4f,1f,2f,3f,4f, 1f,2f,3f,4f,f1,f2,f3,f4,f1,f2,f3,f4,f1,f2,f3,f4,0,0,0,1f,0,0,0,0,0,0,0,0,0,
  //   0,0,0, 0,0,0,0,0,0,0,0,0,0,f1,f2,f3,f4,f6,f7,1f,2f,3f,4f,6f,7f,0,0,18,28,38,48,18,28,38, 48,
  //   18,18,18,28,28,28,38,38,38,48,48,48,18,18,18,28,28,28,38,38,38,48,48,48,18,28, 38,48,18,28,
  //   38,48,18,18,18,28,28,28,38,38,38,48,48,48,18,18,18,28,28,28,38,38,38, 48,48,48,18,28,38,48,
  //   18,18,18,28,28,28,38,38,38,48,48,48,18,18,18,28,28,28,38,38, 38,48,48,48,18,18,18,28,28,28,
  //   38,38,38,48,48,48,18,28,38,48,18,28,38,48,0,0,0,0,0, 0,0,0,0,0,0,0,0,0,0,0,0,15,25,35,45,65,
  //   75,12,13,14,21,23,24,31,32,34,41,42,43,61, 62,63,64,71,72,73,74,16,26,36,46,17,27,37,47,0,0,
  //   0,0,0,0,0,0,0,0,0,0,0,0,0,0,0,0, 0,0,e1,d1,91,0,0,0,0,0,0,1f,2f,3f,4f,1f,2f,3f,4f,1f,2f,3f,
  //   4f,f1,f2,f3,f4,f1,f2,f3, f4,f1,f2,f3,f4,0,0,0,1f,0,0,0,0,0,0,0,0,0,0,0,0,0,0,0,0,0,0,0,0,0,
  //   0,f1,f2,f3,f4,f6, f7,1f,2f,3f,4f,6f,7f,0,0,18,28,38,48,18,28,38,48,18,18,18,28,28,28,38,38,
  //   38,48,48, 48,18,18,18,28,28,28,38,38,38,48,48,48,18,28,38,48,18,28,38,48,18,18,18,28,28,28,
  //    38,38,38,48,48,48,18,18,18,28,28,28,38,38,38,48,48,48,18,28,38,48,18,18,18,28,28, 28,38,38,
  //   38,48,48,48,18,18,18,28,28,28,38,38,38,48,48,48,18,18,18,28,28,28,38,38, 38,48,48,48,18,28,
  //   38,48,18,28,38,48,0,0,0,0,0,0,0,0,0,0,0,0,0,0,0,0,0,15,25,35,45, 65,75,12,13,14,21,23,24,31,
  //   32,34,41,42,43,61,62,63,64,71,72,73,74,16,26,36,46,17, 27,37,47,0,0,0,0,0,0,0,0,0,0,0,0,0,0,
  //   0,0,0,0,0,0,e1,d1,91,0,0,0,0,0,0,1f,2f,3f,4f, 1f,2f,3f,4f,1f,2f,3f,4f,f1,f2,f3,f4,f1,f2,f3,
  //   f4,f1,f2,f3,f4,0,0,0,1f,0,0,0,0,0,0, 0,0,0,0,0,0,0,0,0,0,0,0,0,0,0,0,f1,f2,f3,f4,f6,f7,1f,2f,
  //   3f,4f,6f,7f,0,0,18,28,38, 48,18,28,38,48,18,18,18,28,28,28,38,38,38,48,48,48,18,18,18,28,28,
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  //   contents of Stage 2-B (hex, n*v repeats v):
  //   4,4,4,4,4,4,4,4,4,4,4,4,4,4,4,4,4,4,4,4,4,4,4,4,4,4,4,4,4,4,4,4,4,4,4,4,4,4,4,4,4, 4,4,4,4,
  //   4,4,4,4,4,4,4,5,6,7,4,4,4,4,4,4,4,4,4,30,30,30,30,34,34,34,34,38,38,38,38, 30,30,30,30,34,34,
  //   34,34,38,38,38,38,4,4,4,32,48,48,48,24,4,4,4,4,4,4,4,4,4,4,4,4, 4,4,4,4,4,4,2c,2c,2c,2c,2c,
  //   2c,2d,2d,2d,2d,2d,2d,4,4,4,4,4,4,4,4,4,4,4,4,4,4,4,4,4, 4,4,4,4,4,4,4,4,4,4,4,4,4,4,4,4,4,4,
  //   4,4,4,4,4,4,4,4,4,4,4,4,4,4,4,4,4,4,4,4,4,4,4, 4,4,4,4,4,4,4,4,4,4,4,4,4,4,4,4,4,4,4,4,4,4,
  //   4,4,4,4,4,4,4,4,4,4,4,4,4,4,4,4,4,4,4, 4,4,4,4,4,4,4,4,4,4,4,4,4,4,4,4,4,4,4,4,4,4,4,4,4,4,
  //   4,4,4,4,4,4,4,4,4,4,4,4,4,4,4, 4,4,4,4,4,4,4,4,4,4,4,4,4,4,4,4,4,4,4,4,4,4,4,4,4,4,4,4,4,4,
  //   4,4,4,4,4,4,4,4,4,4,4, 4,5,6,7,4,4,4,4,4,4,4,4,4,30,30,30,30,34,34,34,34,38,38,38,38,30,30,
  //   30,30,34,34,34, 34,38,38,38,38,4,4,4,32,48,48,48,24,4,4,4,4,4,4,4,4,4,4,4,4,4,4,4,4,4,4,2c,
  //   2c,2c, 2c,2c,2c,2d,2d,2d,2d,2d,2d,4,4,4,4,4,4,4,4,4,4,4,4,4,4,4,4,4,4,4,4,4,4,4,4,4,4,4, 4,
  //   4,4,4,4,4,4,4,4,4,4,4,4,4,4,4,4,4,4,4,4,4,4,4,4,4,4,4,4,4,4,4,4,4,4,4,4,4,4,4,4, 4,4,4,4,4,
  //   4,4,4,4,4,4,4,4,4,4,4,4,4,4,4,4,4,4,4,4,4,4,4,4,4,4,4,4,4,4,4,4,4,4,4,4, 4,4,4,4,4,4,4,4,4,
  //   4,4,4,4,4,4,4,4,4,4,4,4,4,4,4,4,4,4,4,4,4,4,4,4,4,4,4,4,4,4,4,4, 4,4,4,4,4,4,4,4,4,4,4,4,4,
  //   4,4,4,4,4,4,4,4,4,4,4,4,4,4,4,4,4,4,4,5,6,7,4,4,4,4,4,4, 4,4,4,30,30,30,30,34,34,34,34,38,38,
  //   38,38,30,30,30,30,34,34,34,34,38,38,38,38,4,4, 4,32,48,48,48,24,4,4,4,4,4,4,4,4,4,4,4,4,4,4,
  //   4,4,4,4,2c,2c,2c,2c,2c,2c,2d,2d,2d,2d, 2d,2d,4,4,4,4,4,4,4,4,4,4,4,4,4,4,4,4,4,4,4,4,4,4,4,
  //   4,4,4,4,4,4,4,4,4,4,4,4,4,4,4, 4,4,4,4,4,4,4,4,4,4,4,4,4,4,4,4,4,4,4,4,4,4,4,4,4,4,4,4,4,4,
  //   4,4,4,4,4,4,4,4,4,4,4, 4,4,4,4,4,4,4,4,4,4,4,4,4,4,4,4,4,4,4,4,4,4,4,4,4,4,4,4,4,4,4,4,4,4,
  //   4,4,4,4,4,4,4, 4,4,4,4,4,4,4,4,4,4,4,4,4,4,4,4,4,4,4,4,4,4,4,4,4,4,4,4,4,4,4,4,4,4,4,4,4,4,
  //   4,4,4, 4,4,4,4,4,4,4,4,4,4,4,4,4,4,4,4,4,4,4,4,4,5,6,7,4,4,4,4,4,4,4,4,4,30,30,30,30,34, 34,
  //   34,34,38,38,38,38,30,30,30,30,34,34,34,34,38,38,38,38,4,4,4,32,48,48,48,24,4,4, 4,4,4,4,4,4,
  //   4,4,4,4,4,4,4,4,4,4,2c,2c,2c,2c,2c,2c,2d,2d,2d,2d,2d,2d,4,4,4,4,4,4,4, 4,4,4,4,4,4,4,4,4,4,
  //   4,4,4,4,4,4,4,4,4,4,4,4,4,4,4,4,4,4,4,4,4,4,4,4,4,4,4,4,4,4,4, 4,4,4,4,4,4,4,4,4,4,4,4,4,4,
  //   4,4,4,4,4,4,4,4,4,4,4,4,4,4,4,4,4,4,4,4,4,4,4,4,4,4,4, 4,4,4,4,4,4,4,4,4,4,4,4,4,4,4,4,4,4,
  //   4,4,4,4,4,4,4,4,4,4,4,4,4,4,4,4,4,4,4,4,4,4,4, 4,4,4,4,4,4,4,4,4,4,4,4,4,4,4,4,4,4,4,4,4,4,
  //   4,4,4,4,4,4,4,4,4,4,4,4,4,4,4,4,4,4,4, 4,4,4,4,4,4,4,4,4,4,4,5,6,7,4,4,4,4,4,4,4,4,4,30,30,
  //   30,30,34,34,34,34,38,38,38,38, 30,30,30,30,34,34,34,34,38,38,38,38,4,4,4,32,48,48,48,24,4,4,
  //   4,4,4,4,4,4,4,4,4,4, 4,4,4,4,4,4,2c,2c,2c,2c,2c,2c,2d,2d,2d,2d,2d,2d,4,4,4,4,4,4,4,4,4,4,4,
  //   4,4,4,4,4,4, 4,4,4,4,4,4,4,4,4,4,4,4,4,4,4,4,4,4,4,4,4,4,4,4,4,4,4,4,4,4,4,4,4,4,4,4,4,4,4,
  //   4,4, 4,4,4,4,4,4,4,4,4,4,4,4,4,4,4,4,4,4,4,4,4,4,4,4,4,4,4,4,4,4,4,4,4,4,4,4,4,4,4,4,4, 4,4,
  //   4,4,4,4,4,4,4,4,4,4,4,4,4,4,4,4,4,4,4,4,4,4,4,4,4,4,4,4,4,4,4,4,4,4,4,4,4,4,4, 4,4,4,4,4,4,
  //   4,4,4,4,4,4,4,4,4,4,4,4,4,4,4,4,4,4,4,4,4,4,4,4,4,4,4,4,4,4,4,4,4,4,4, 4,5,6,7,4,4,4,4,4,4,
  //   4,4,4,30,30,30,30,34,34,34,34,38,38,38,38,30,30,30,30,34,34,34, 34,38,38,38,38,4,4,4,32,48,
  //   48,48,24,4,4,4,4,4,4,4,4,4,4,4,4,4,4,4,4,4,4,2c,2c,2c, 2c,2c,2c,2d,2d,2d,2d,2d,2d,4,4,4,4,4,
  //   4,4,4,4,4,4,4,4,4,4,4,4,4,4,4,4,4,4,4,4,4,4, 4,4,4,4,4,4,4,4,4,4,4,4,4,4,4,4,4,4,4,4,4,4,4,
  //   4,4,4,4,4,4,4,4,4,4,4,4,4,4,4,4,4,4, 4,4,4,4,4,4,4,4,4,4,4,4,4,4,4,4,4,4,4,4,4,4,4,4,4,4,4,
  //   4,4,4,4,4,4,4,4,4,4,4,4,4,4, 4,4,4,4,4,4,4,4,4,4,4,4,4,4,4,4,4,4,4,4,4,4,4,4,4,4,4,4,4,4,4,
  //   4,4,4,4,4,4,4,4,4,4, 4,4,4,4,4,4,4,4,4,4,4,4,4,4,4,4,4,4,4,4,4,4,4,4,4,4,4,4,4,4,4,4,5,6,7,
  //   4,4,4,4,4,4, 4,4,4,30,30,30,30,34,34,34,34,38,38,38,38,30,30,30,30,34,34,34,34,38,38,38,38,
  //   4,4, 4,32,48,48,48,24,4,4,4,4,4,4,4,4,4,4,4,4,4,4,4,4,4,4,2c,2c,2c,2c,2c,2c,2d,2d,2d,2d, 2d,
  //   2d,4,4,4,4,4,4,4,4,4,4,4,4,4,4,4,4,4,4,4,4,4,4,4,4,4,4,4,4,4,4,4,4,4,4,4,4,4,4, 4,4,4,4,4,4,
  //   4,4,4,4,4,4,4,4,4,4,4,4,4,4,4,4,4,4,4,4,4,4,4,4,4,4,4,4,4,4,4,4,4,4,4, 4,4,4,4,4,4,4,4,4,4,
  //   4,4,4,4,4,4,4,4,4,4,4,4,4,4,4,4,4,4,4,4,4,4,4,4,4,4,4,4,4,4,4, 4,4,4,4,4,4,4,4,4,4,4,4,4,4,
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  //   contents of Stage 1-A (hex, n*v repeats v):
  //   0,0,0,0,0,0,0,0,0,0,0,0,0,0,0,0,0,0,0,0,0,0,0,0,0,0,0,0,0,0,0,0,0,0,0,0,0,0,0,0,0, 0,0,0,0,
  //   0,0,0,0,0,0,0,0,0,0,0,0,0,0,0,0,0,0,0,0,0,0,0,0,0,0,0,0,0,0,0,0,0,0,0,0,0, 0,0,0,0,0,0,0,0,
  //   0,0,0,0,0,0,0,0,0,0,0,0,0,0,0,0,0,0,0,0,0,0,0,0,0,0,0,0,0,0,0,0,0, 0,0,0,0,e0,10,15,1a,1f,20,
  //   25,2a,2f,34,38,3c,31,39,3d,32,36,3e,33,37,3b,44,48,4c,41, 49,4d,42,46,4e,43,47,4b,50,55,5a,
  //   5f,60,65,6a,6f,74,78,7c,71,79,7d,72,76,7e,73,77, 7b,84,88,8c,81,89,8d,82,86,8e,83,87,8b,90,
  //   95,9a,9f,a4,a8,ac,a1,a9,ad,a2,a6,ae,a3, a7,ab,b4,b8,bc,b1,b9,bd,b2,b6,be,b3,b7,bb,c4,c8,cc,
  //   c1,c9,cd,c2,c6,ce,c3,c7,cb,c0, c5,ca,cf,d0,d5,da,df,74,78,7c,71,79,7d,72,76,7e,73,77,7b,a0,
  //   a5,aa,af,0,0,0,0,0,0, 0,0,0,0,0,0,0,0,0,0,0,0,0,0,0,0,0,0,0,0,0,0,0,0,0,0,0,0,0,0,0,0,0,0,0,
  //   0,0,0,0,0,0, 0,0,0,0,0,0,0,0,0,0,0,0,0,0,0,0,0,0,0,0,0,0,0,0,0,0,0,0,0,0,0,0,0,0,0,0,0,0,0,
  //   0,0, 0,0,0,0,0,0,0,0,0,0,0,0,0,0,0,0,0,0,0,0,0,0,0,0,0,0,0,0,0,0,0,0,0,0,0,0,0,0,0,e0, 10,15,
  //   1a,1f,20,25,2a,2f,34,38,3c,31,39,3d,32,36,3e,33,37,3b,44,48,4c,41,49,4d,42, 46,4e,43,47,4b,
  //   50,55,5a,5f,60,65,6a,6f,74,78,7c,71,79,7d,72,76,7e,73,77,7b,84,88, 8c,81,89,8d,82,86,8e,83,
  //   87,8b,90,95,9a,9f,a4,a8,ac,a1,a9,ad,a2,a6,ae,a3,a7,ab,b4, b8,bc,b1,b9,bd,b2,b6,be,b3,b7,bb,
  //   c4,c8,cc,c1,c9,cd,c2,c6,ce,c3,c7,cb,c0,c5,ca,cf, d0,d5,da,df,74,78,7c,71,79,7d,72,76,7e,73,
  //   77,7b,a0,a5,aa,af,0,0,0,0,0,0,0,0,0,0,0, 0,0,0,0,0,0,0,0,0,0,0,0,0,0,0,0,0,0,0,0,0,0,0,0,0,
  //   0,0,0,0,0,0,0,0,0,0,0,0,0,0,0,0, 0,0,0,0,0,0,0,0,0,0,0,0,0,0,0,0,0,0,0,0,0,0,0,0,0,0,0,0,0,
  //   0,0,0,0,0,0,0,0,0,0,0,0, 0,0,0,0,0,0,0,0,0,0,0,0,0,0,0,0,0,0,0,0,0,0,0,0,0,0,0,0,0,0,0,0,0,
  //   0,e0,10,15,1a,1f, 20,25,2a,2f,34,38,3c,31,39,3d,32,36,3e,33,37,3b,44,48,4c,41,49,4d,42,46,4e,
  //   43,47, 4b,50,55,5a,5f,60,65,6a,6f,74,78,7c,71,79,7d,72,76,7e,73,77,7b,84,88,8c,81,89,8d, 82,
  //   86,8e,83,87,8b,90,95,9a,9f,a4,a8,ac,a1,a9,ad,a2,a6,ae,a3,a7,ab,b4,b8,bc,b1,b9, bd,b2,b6,be,
  //   b3,b7,bb,c4,c8,cc,c1,c9,cd,c2,c6,ce,c3,c7,cb,c0,c5,ca,cf,d0,d5,da,df, 74,78,7c,71,79,7d,72,
  //   76,7e,73,77,7b,a0,a5,aa,af,0,0,0,0,0,0,0,0,0,0,0,0,0,0,0,0,0, 0,0,0,0,0,0,0,0,0,0,0,0,0,0,0,
  //   0,0,0,0,0,0,0,0,0,0,0,0,0,0,0,0,0,0,0,0,0,0,0,0,0,0, 0,0,0,0,0,0,0,0,0,0,0,0,0,0,0,0,0,0,0,
  //   0,0,0,0,0,0,0,0,0,0,0,0,0,0,0,0,0,0,0,0,0,0, 0,0,0,0,0,0,0,0,0,0,0,0,0,0,0,0,0,0,0,0,0,0,0,
  //   0,0,0,0,0,e0,10,15,1a,1f,20,25,2a,2f, 34,38,3c,31,39,3d,32,36,3e,33,37,3b,44,48,4c,41,49,4d,
  //   42,46,4e,43,47,4b,50,55,5a, 5f,60,65,6a,6f,74,78,7c,71,79,7d,72,76,7e,73,77,7b,84,88,8c,81,
  //   89,8d,82,86,8e,83, 87,8b,90,95,9a,9f,a4,a8,ac,a1,a9,ad,a2,a6,ae,a3,a7,ab,b4,b8,bc,b1,b9,bd,
  //   b2,b6,be, b3,b7,bb,c4,c8,cc,c1,c9,cd,c2,c6,ce,c3,c7,cb,c0,c5,ca,cf,d0,d5,da,df,74,78,7c,71,
  //    79,7d,72,76,7e,73,77,7b,a0,a5,aa,af,0,0,0,0,0,0,0,0,0,0,0,0,0,0,0,0,0,0,0,0,0,0,0, 0,0,0,0,
  //   0,0,0,0,0,0,0,0,0,0,0,0,0,0,0,0,0,0,0,0,0,0,0,0,0,0,0,0,0,0,0,0,0,0,0,0,0, 0,0,0,0,0,0,0,0,
  //   0,0,0,0,0,0,0,0,0,0,0,0,0,0,0,0,0,0,0,0,0,0,0,0,0,0,0,0,0,0,0,0,0, 0,0,0,0,0,0,0,0,0,0,0,0,
  //   0,0,0,0,0,0,0,0,0,0,e0,10,15,1a,1f,20,25,2a,2f,34,38,3c,31, 39,3d,32,36,3e,33,37,3b,44,48,4c,
  //   41,49,4d,42,46,4e,43,47,4b,50,55,5a,5f,60,65,6a, 6f,74,78,7c,71,79,7d,72,76,7e,73,77,7b,84,
  //   88,8c,81,89,8d,82,86,8e,83,87,8b,90,95, 9a,9f,a4,a8,ac,a1,a9,ad,a2,a6,ae,a3,a7,ab,b4,b8,bc,
  //   b1,b9,bd,b2,b6,be,b3,b7,bb,c4, c8,cc,c1,c9,cd,c2,c6,ce,c3,c7,cb,c0,c5,ca,cf,d0,d5,da,df,74,
  //   78,7c,71,79,7d,72,76, 7e,73,77,7b,a0,a5,aa,af,0,0,0,0,0,0,0,0,0,0,0,0,0,0,0,0,0,0,0,0,0,0,0,
  //   0,0,0,0,0,0, 0,0,0,0,0,0,0,0,0,0,0,0,0,0,0,0,0,0,0,0,0,0,0,0,0,0,0,0,0,0,0,0,0,0,0,0,0,0,0,
  //   0,0, 0,0,0,0,0,0,0,0,0,0,0,0,0,0,0,0,0,0,0,0,0,0,0,0,0,0,0,0,0,0,0,0,0,0,0,0,0,0,0,0,0, 0,0,
  //   0,0,0,0,0,0,0,0,0,0,0,0,0,0,e0,10,15,1a,1f,20,25,2a,2f,34,38,3c,31,39,3d,32,36, 3e,33,37,3b,
  //   44,48,4c,41,49,4d,42,46,4e,43,47,4b,50,55,5a,5f,60,65,6a,6f,74,78,7c, 71,79,7d,72,76,7e,73,
  //   77,7b,84,88,8c,81,89,8d,82,86,8e,83,87,8b,90,95,9a,9f,a4,a8, ac,a1,a9,ad,a2,a6,ae,a3,a7,ab,
  //   b4,b8,bc,b1,b9,bd,b2,b6,be,b3,b7,bb,c4,c8,cc,c1,c9, cd,c2,c6,ce,c3,c7,cb,c0,c5,ca,cf,d0,d5,
  //   da,df,74,78,7c,71,79,7d,72,76,7e,73,77,7b, a0,a5,aa,af,0,0,0,0,0,0,0,0,0,0,0,0,0,0,0,0,0,0,
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endmodule
